// Logisim project main - Copy.circ as structural Verilog: 1 circuit, main circuit main
module main (
  input  in_1,
  input  in_2,
  input  in_3,
  input  in_4
);

  wire and_1_out, and_2_out, and_3_out, and_4_out, and_5_out, and_6_out, and_7_out, and_8_out, and_9_out,
       and_10_out, and_11_out, and_12_out, and_13_out, and_14_out, clock_1_out, multiplexer_1_out,
       multiplexer_2_out, multiplexer_3_out, multiplexer_4_out, multiplexer_5_out, multiplexer_6_out,
       multiplexer_7_out, not_1_out, not_2_out, or_1_out, or_2_out, or_3_out, or_4_out, or_5_out, t_ff_1_qn,
       t_ff_2_qn, t_ff_3_qn, t_ff_4_q, t_ff_4_qn;
  wire [2:0] t_ff_3_q;

  not not_1 (not_1_out, t_ff_4_q);
  Multiplexer #(.select(3), .enable("false")) multiplexer_1 (
    .in0(in_3), .in1(t_ff_4_q), .in2(t_ff_4_q), .in3(in_3), .in4(in_3), .in5(in_4), .in6(not_1_out),
    .in7(in_4), .out(multiplexer_1_out), .sel(t_ff_3_q));
  Multiplexer #(.select(3), .enable("false")) multiplexer_2 (
    .in0(t_ff_4_q), .in1(in_3), .in2(in_4), .in3(in_4), .in4(in_3), .in5(not_1_out), .in6(not_1_out),
    .in7(in_4), .out(multiplexer_2_out), .sel(t_ff_3_q));
  Multiplexer #(.select(3), .enable("false")) multiplexer_3 (
    .in0(not_1_out), .in1(in_3), .in2(in_4), .in3(not_1_out), .in4(t_ff_4_q), .in5(not_1_out),
    .in6(not_1_out), .in7(in_4), .out(multiplexer_3_out), .sel(t_ff_3_q));
  Multiplexer #(.select(3), .enable("false")) multiplexer_4 (
    .in0(not_1_out), .in1(t_ff_4_q), .in2(t_ff_4_q), .in3(in_3), .in4(in_3), .in5(in_4), .in6(in_4),
    .in7(in_4), .out(multiplexer_4_out), .sel(t_ff_3_q));
  Multiplexer #(.select(3), .enable("false")) multiplexer_5 (
    .in0(t_ff_4_q), .in1(t_ff_4_q), .in2(t_ff_4_q), .in3(t_ff_4_q), .in4(not_1_out), .in5(in_4), .in6(in_4),
    .in7(in_4), .out(multiplexer_5_out), .sel(t_ff_3_q));
  Multiplexer #(.select(3), .enable("false")) multiplexer_6 (
    .in0(in_3), .in1(t_ff_4_q), .in2(t_ff_4_q), .in3(in_3), .in4(in_4), .in5(in_4), .in6(in_4), .in7(in_4),
    .out(multiplexer_6_out), .sel(t_ff_3_q));
  Multiplexer #(.select(3), .enable("false")) multiplexer_7 (
    .in0(in_3), .in1(t_ff_4_q), .in2(not_1_out), .in3(in_3), .in4(in_3), .in5(t_ff_4_q), .in6(in_4),
    .in7(in_4), .out(multiplexer_7_out), .sel(t_ff_3_q));
  Clock clock_1 (.out(clock_1_out));
  _7_Segment_Display u_7_segment_display_1 (
    .g(multiplexer_7_out), .f(multiplexer_6_out), .a(multiplexer_1_out), .b(multiplexer_2_out),
    .e(multiplexer_5_out), .d(multiplexer_4_out), .c(multiplexer_3_out));  // open: dp
  and and_1 (and_1_out, clock_1_out, in_2);
  T_Flip_Flop t_ff_1 (.clk(and_1_out), .T(or_2_out), .Q(t_ff_3_q[2]), .Qn(t_ff_1_qn));  // open: preset, reset, en
  T_Flip_Flop t_ff_2 (.clk(and_1_out), .T(or_3_out), .Q(t_ff_3_q[1]), .Qn(t_ff_2_qn));  // open: preset, reset, en
  T_Flip_Flop t_ff_3 (.clk(and_1_out), .T(or_4_out), .Q(t_ff_3_q[0]), .Qn(t_ff_3_qn));  // open: preset, reset, en
  T_Flip_Flop t_ff_4 (.clk(and_1_out), .T(or_5_out), .Q(t_ff_4_q), .Qn(t_ff_4_qn));  // open: preset, reset, en
  not not_2 (not_2_out, in_1);
  and and_2 (and_2_out, in_1, t_ff_2_qn, t_ff_3_qn, t_ff_4_qn);
  and and_3 (and_3_out, not_2_out, t_ff_3_q[1], t_ff_3_q[0], t_ff_4_q);
  and and_4 (and_4_out, not_2_out, t_ff_3_q[2], t_ff_3_q[1]);
  and and_5 (and_5_out, in_1, t_ff_3_qn, t_ff_4_qn);
  and and_6 (and_6_out, not_2_out, t_ff_3_q[0], t_ff_4_q);
  and and_7 (and_7_out, t_ff_3_q[2], t_ff_3_q[1]);
  and and_8 (and_8_out, in_1, t_ff_3_q[0], t_ff_4_qn);
  and and_9 (and_9_out, in_1, t_ff_3_q[1], t_ff_4_qn);
  and and_10 (and_10_out, in_1, t_ff_3_q[2], t_ff_4_qn);
  and and_11 (and_11_out, not_2_out, t_ff_4_q);
  and and_12 (and_12_out, not_2_out, t_ff_2_qn);
  and and_13 (and_13_out, t_ff_1_qn, t_ff_3_q[1]);
  and and_14 (and_14_out, in_1, t_ff_3_q[2]);
  or or_1 (or_1_out, and_12_out, and_13_out, and_14_out, t_ff_4_q);
  or or_2 (or_2_out, and_2_out, and_3_out, and_4_out);
  or or_3 (or_3_out, and_5_out, and_6_out, and_7_out);
  or or_4 (or_4_out, and_8_out, and_9_out, and_10_out, and_11_out);
  or or_5 (or_5_out, or_1_out, t_ff_3_q[0]);
endmodule
