// Logisim project main.circ as structural Verilog: 1 circuit, main circuit main
module main (
  input  in_1,
  input  in_2,
  input  in_3,
  input  in_4
);

  wire and_1_out, and_2_out, and_3_out, and_4_out, and_5_out, and_6_out, and_7_out, and_8_out, and_9_out,
       and_10_out, and_11_out, and_12_out, and_13_out, and_14_out, and_15_out, and_16_out, and_17_out,
       and_18_out, and_19_out, and_20_out, and_21_out, and_22_out, and_23_out, clock_1_out, d_ff_1_qn,
       d_ff_2_qn, d_ff_3_qn, d_ff_4_q, d_ff_4_qn, multiplexer_1_out, multiplexer_2_out, multiplexer_3_out,
       multiplexer_4_out, multiplexer_5_out, multiplexer_6_out, multiplexer_7_out, not_1_out, not_2_out,
       or_1_out, or_2_out, or_3_out, or_4_out, or_5_out, or_6_out, or_7_out, or_8_out;
  wire [2:0] d_ff_3_q;

  not not_1 (not_1_out, d_ff_4_q);
  Multiplexer #(.select(3), .enable("false")) multiplexer_1 (
    .in0(in_3), .in1(d_ff_4_q), .in2(d_ff_4_q), .in3(in_3), .in4(in_3), .in5(in_4), .in6(not_1_out),
    .in7(in_4), .out(multiplexer_1_out), .sel(d_ff_3_q));
  Multiplexer #(.select(3), .enable("false")) multiplexer_2 (
    .in0(d_ff_4_q), .in1(in_3), .in2(in_4), .in3(in_4), .in4(in_3), .in5(not_1_out), .in6(not_1_out),
    .in7(in_4), .out(multiplexer_2_out), .sel(d_ff_3_q));
  Multiplexer #(.select(3), .enable("false")) multiplexer_3 (
    .in0(not_1_out), .in1(in_3), .in2(in_4), .in3(not_1_out), .in4(d_ff_4_q), .in5(not_1_out),
    .in6(not_1_out), .in7(in_4), .out(multiplexer_3_out), .sel(d_ff_3_q));
  Multiplexer #(.select(3), .enable("false")) multiplexer_4 (
    .in0(not_1_out), .in1(d_ff_4_q), .in2(d_ff_4_q), .in3(in_3), .in4(in_3), .in5(in_4), .in6(in_4),
    .in7(in_4), .out(multiplexer_4_out), .sel(d_ff_3_q));
  Multiplexer #(.select(3), .enable("false")) multiplexer_5 (
    .in0(d_ff_4_q), .in1(d_ff_4_q), .in2(d_ff_4_q), .in3(d_ff_4_q), .in4(not_1_out), .in5(in_4), .in6(in_4),
    .in7(in_4), .out(multiplexer_5_out), .sel(d_ff_3_q));
  Multiplexer #(.select(3), .enable("false")) multiplexer_6 (
    .in0(in_3), .in1(d_ff_4_q), .in2(d_ff_4_q), .in3(in_3), .in4(in_4), .in5(in_4), .in6(in_4), .in7(in_4),
    .out(multiplexer_6_out), .sel(d_ff_3_q));
  Multiplexer #(.select(3), .enable("false")) multiplexer_7 (
    .in0(in_3), .in1(d_ff_4_q), .in2(not_1_out), .in3(in_3), .in4(in_3), .in5(d_ff_4_q), .in6(in_4),
    .in7(in_4), .out(multiplexer_7_out), .sel(d_ff_3_q));
  Clock clock_1 (.out(clock_1_out));
  _7_Segment_Display u_7_segment_display_1 (
    .g(multiplexer_7_out), .f(multiplexer_6_out), .a(multiplexer_1_out), .b(multiplexer_2_out),
    .e(multiplexer_5_out), .d(multiplexer_4_out), .c(multiplexer_3_out));  // open: dp
  and and_1 (and_1_out, clock_1_out, in_2);
  D_Flip_Flop d_ff_1 (.clk(and_1_out), .D(or_8_out), .Q(d_ff_3_q[2]), .Qn(d_ff_1_qn));  // open: preset, en, reset
  D_Flip_Flop d_ff_2 (.clk(and_1_out), .D(or_5_out), .Q(d_ff_3_q[1]), .Qn(d_ff_2_qn));  // open: preset, en, reset
  D_Flip_Flop d_ff_3 (.clk(and_1_out), .D(or_6_out), .Q(d_ff_3_q[0]), .Qn(d_ff_3_qn));  // open: preset, en, reset
  D_Flip_Flop d_ff_4 (.clk(and_1_out), .D(or_7_out), .Q(d_ff_4_q), .Qn(d_ff_4_qn));  // open: preset, en, reset
  not not_2 (not_2_out, in_1);
  and and_2 (and_2_out, in_1, d_ff_1_qn, d_ff_2_qn, d_ff_3_qn);
  and and_3 (and_3_out, in_1, d_ff_3_q[2], d_ff_3_q[1], d_ff_3_qn);
  and and_4 (and_4_out, not_2_out, d_ff_3_q[1], d_ff_3_q[0], d_ff_4_q);
  and and_5 (and_5_out, not_2_out, d_ff_3_q[2], d_ff_2_qn);
  and and_6 (and_6_out, d_ff_3_q[2], d_ff_2_qn, d_ff_4_q);
  and and_7 (and_7_out, d_ff_3_q[2], d_ff_2_qn, d_ff_3_q[0]);
  and and_8 (and_8_out, not_2_out, d_ff_1_qn, d_ff_3_q[1], d_ff_4_qn);
  and and_9 (and_9_out, in_1, d_ff_2_qn, d_ff_3_qn, d_ff_4_qn);
  and and_10 (and_10_out, not_2_out, d_ff_2_qn, d_ff_3_q[0], d_ff_4_q);
  and and_11 (and_11_out, d_ff_3_q[1], d_ff_3_qn, d_ff_4_q);
  and and_12 (and_12_out, in_1, d_ff_3_q[1], d_ff_3_q[0]);
  and and_13 (and_13_out, in_1, d_ff_3_q[1], d_ff_3_qn, d_ff_4_qn);
  and and_14 (and_14_out, in_1, d_ff_3_q[2], d_ff_3_qn, d_ff_4_qn);
  and and_15 (and_15_out, not_2_out, d_ff_3_qn, d_ff_4_q);
  and and_16 (and_16_out, not_2_out, d_ff_3_q[0], d_ff_4_qn);
  and and_17 (and_17_out, in_1, d_ff_3_q[0], d_ff_4_q);
  and and_18 (and_18_out, not_2_out, d_ff_2_qn, d_ff_4_qn);
  and and_19 (and_19_out, d_ff_1_qn, d_ff_3_q[1], d_ff_4_qn);
  and and_20 (and_20_out, in_1, d_ff_3_q[2], d_ff_4_qn);
  and and_21 (and_21_out, d_ff_3_q[0], d_ff_4_qn);
  and and_22 (and_22_out, and_2_out, d_ff_4_qn);
  and and_23 (and_23_out, and_3_out, d_ff_4_qn);
  or or_1 (or_1_out, and_6_out, and_7_out);
  or or_2 (or_2_out, and_13_out, and_14_out, and_15_out, and_16_out);
  or or_3 (or_3_out, and_22_out, and_23_out, and_4_out, and_5_out);
  or or_4 (or_4_out, and_8_out, and_9_out, and_10_out, and_11_out);
  or or_5 (or_5_out, or_4_out, and_12_out);
  or or_6 (or_6_out, or_2_out, and_17_out);
  or or_7 (or_7_out, and_18_out, and_19_out, and_20_out, and_21_out);
  or or_8 (or_8_out, or_3_out, or_1_out);
endmodule
