// Logisim project partB.circ as structural Verilog: 1 circuit, main circuit main
module main (
  input  in_1,
  input  [3:0] in_2,
  output a,
  output b,
  output c,
  output d,
  output e,
  output f,
  output g
);

  wire decoder_1_out0, decoder_1_out1, decoder_1_out2, decoder_1_out3, decoder_1_out4, decoder_1_out5,
       decoder_1_out6, decoder_1_out7, decoder_1_out8, decoder_1_out9, decoder_1_out10, decoder_1_out11,
       decoder_1_out12;

  Decoder #(.select(4)) decoder_1 (
    .out0(decoder_1_out0), .out1(decoder_1_out1), .out2(decoder_1_out2), .out3(decoder_1_out3),
    .out4(decoder_1_out4), .out5(decoder_1_out5), .out6(decoder_1_out6), .out7(decoder_1_out7),
    .out8(decoder_1_out8), .out9(decoder_1_out9), .out10(decoder_1_out10), .out11(decoder_1_out11),
    .out12(decoder_1_out12), .sel(in_2), .en(in_1));  // open: out13, out14, out15
  or or_1 (e, decoder_1_out1, decoder_1_out3, decoder_1_out5, decoder_1_out7, decoder_1_out8);
  or or_2 (f, decoder_1_out0, decoder_1_out1, decoder_1_out3, decoder_1_out5, decoder_1_out6, decoder_1_out7);
  or or_3 (g, decoder_1_out0, decoder_1_out1, decoder_1_out3, decoder_1_out4, decoder_1_out6, decoder_1_out7, decoder_1_out8, decoder_1_out9, decoder_1_out11);
  or or_4 (b, decoder_1_out1, decoder_1_out2, decoder_1_out3, decoder_1_out8, decoder_1_out9, decoder_1_out10, decoder_1_out12);
  or or_5 (c, decoder_1_out0, decoder_1_out2, decoder_1_out3, decoder_1_out6, decoder_1_out9, decoder_1_out10, decoder_1_out12);
  or or_6 (d, decoder_1_out0, decoder_1_out3, decoder_1_out5, decoder_1_out6, decoder_1_out7, decoder_1_out8, decoder_1_out9);
  or or_7 (a, decoder_1_out0, decoder_1_out1, decoder_1_out3, decoder_1_out5, decoder_1_out6, decoder_1_out7, decoder_1_out8, decoder_1_out9, decoder_1_out12);
  _7_Segment_Display u_7_segment_display_1 (.g(g), .f(f), .a(a), .b(b), .e(e), .d(d), .c(c));  // open: dp
endmodule
