// Logisim project partC-MUX.circ as structural Verilog: 1 circuit, main circuit main
module main (
  input  [2:0] in_1,
  input  in_2,
  input  in_3,
  input  in_4
);

  wire multiplexer_1_out, multiplexer_2_out, multiplexer_3_out, multiplexer_4_out, multiplexer_5_out,
       multiplexer_6_out, multiplexer_7_out, not_1_out;

  not not_1 (not_1_out, in_2);
  Multiplexer #(.select(3), .enable("false")) multiplexer_1 (
    .in0(in_4), .in1(in_2), .in2(in_2), .in3(in_4), .in4(in_4), .in5(in_3), .in6(not_1_out), .in7(in_3),
    .out(multiplexer_1_out), .sel(in_1));
  Multiplexer #(.select(3), .enable("false")) multiplexer_2 (
    .in0(in_2), .in1(in_4), .in2(in_3), .in3(in_3), .in4(in_4), .in5(not_1_out), .in6(not_1_out), .in7(in_3),
    .out(multiplexer_2_out), .sel(in_1));
  Multiplexer #(.select(3), .enable("false")) multiplexer_3 (
    .in0(not_1_out), .in1(in_4), .in2(in_3), .in3(not_1_out), .in4(in_2), .in5(not_1_out), .in6(not_1_out),
    .in7(in_3), .out(multiplexer_3_out), .sel(in_1));
  Multiplexer #(.select(3), .enable("false")) multiplexer_4 (
    .in0(not_1_out), .in1(in_2), .in2(in_2), .in3(in_4), .in4(in_4), .in5(in_3), .in6(in_3), .in7(in_3),
    .out(multiplexer_4_out), .sel(in_1));
  Multiplexer #(.select(3), .enable("false")) multiplexer_5 (
    .in0(in_2), .in1(in_2), .in2(in_2), .in3(in_2), .in4(not_1_out), .in5(in_3), .in6(in_3), .in7(in_3),
    .out(multiplexer_5_out), .sel(in_1));
  Multiplexer #(.select(3), .enable("false")) multiplexer_6 (
    .in0(in_4), .in1(in_2), .in2(in_2), .in3(in_4), .in4(in_3), .in5(in_3), .in6(in_3), .in7(in_3),
    .out(multiplexer_6_out), .sel(in_1));
  Multiplexer #(.select(3), .enable("false")) multiplexer_7 (
    .in0(in_4), .in1(in_2), .in2(not_1_out), .in3(in_4), .in4(in_4), .in5(in_2), .in6(in_3), .in7(in_3),
    .out(multiplexer_7_out), .sel(in_1));
  _7_Segment_Display u_7_segment_display_1 (
    .g(multiplexer_7_out), .f(multiplexer_6_out), .a(multiplexer_1_out), .b(multiplexer_2_out),
    .e(multiplexer_5_out), .d(multiplexer_4_out), .c(multiplexer_3_out));  // open: dp
endmodule
